// Logisim project cpu.circ as structural Verilog
module main (
  input  [31:0] INSTRUCTION,
  input  CLOCK,
  output [31:0] FETCH_ADDRESS,
  output [31:0] ra_Value,
  output [31:0] sp_Value,
  output [31:0] t0_Value,
  output [31:0] t1_Value,
  output [31:0] t2_Value,
  output [31:0] s0_Value,
  output [31:0] s1_Value,
  output [31:0] a0_Value
);

  wire ASel, BrEq, BrLt, BrUn, BSel, isFirstOp, isLB, isLH, isLW, isSW, isSWGE, load, MemRW, MemRW_TBD,
       PCSel, RegWEn, store;
  wire [1:0] WBSel;
  wire [2:0] ImmSel;
  wire [3:0] ALUSel;
  wire [31:0] adder_2_out, alu_output, imm, instruction_t, mem, multiplexer_1_out, multiplexer_2_out,
       multiplexer_3_out, multiplexer_4_out, multiplexer_5_out, pc, pc_4, PC_q, read_data_1, read_data_2,
       shifter_2_out, undone_alu_output, write_back;

  Register #(.width(32)) u_PC (.D(multiplexer_1_out), .Q(PC_q), .clk(CLOCK));  // open: en, clr
  Multiplexer #(.width(32), .enable("false")) multiplexer_1 (
    .in0(pc_4), .in1(alu_output), .out(multiplexer_1_out), .sel(PCSel));
  Adder #(.width(32)) adder_1 (.a(32'h4), .b(PC_q), .out(pc_4));  // open: cin, cout
  Shifter #(.width(32), .shift("lr")) shifter_1 (.in(PC_q), .\dist (5'b00010), .out(FETCH_ADDRESS));
  Multiplexer #(.width(32), .enable("false")) multiplexer_2 (
    .in0(INSTRUCTION), .in1({32{1'b0}}), .out(multiplexer_2_out), .sel(PCSel));
  Register #(.width(32)) pc_2 (.D(PC_q), .Q(pc), .clk(CLOCK));  // open: en, clr
  Register #(.width(32)) u_instruction (.D(multiplexer_2_out), .Q(instruction_t), .clk(CLOCK));  // open: en, clr
  ImmGen immgen_1 (._25bit(instruction_t[31:7]), .immSel(ImmSel), .Imm(imm));
  firstOp firstop_1 (.pc(pc), .isItFirst(isFirstOp));
  regfile_main main_1 (
    .Read_Register_1__rs1(instruction_t[19:15]), .Read_Register_2__rs2(instruction_t[24:20]),
    .Write_Register__rd(instruction_t[11:7]), .Write_Data(write_back), .Write_Enable(RegWEn), .Clock(CLOCK),
    .Read_Data_1(read_data_1), .Read_Data_2(read_data_2), .ra_Value(ra_Value), .sp_Value(sp_Value),
    .t0_Value(t0_Value), .t1_Value(t1_Value), .t2_Value(t2_Value), .s0_Value(s0_Value), .s1_Value(s1_Value),
    .a0_Value(a0_Value));
  Control_Panel control_panel_1 (
    .PCSel(PCSel), .instruction(instruction_t), .ImmSel(ImmSel), .RegWEn(RegWEn), .BrEq(BrEq), .BrLt(BrLt),
    .BSel(BSel), .ASel(ASel), .ALUSel(ALUSel), .MemRW_TBD(MemRW_TBD), .WBSel(WBSel), .load(load),
    .store(store), .BrUn(BrUn), .isSWGE(isSWGE), .isSW(isSW), .isLB(isLB), .isLH(isLH), .isLW(isLW));
  BrChoose brchoose_1 (.read_data_1(read_data_1), .read_data_2(read_data_2), .BrUn(BrUn), .BrEq(BrEq), .BrLt(BrLt));
  Multiplexer #(.width(32), .enable("false")) multiplexer_3 (
    .in0(read_data_1), .in1(pc), .out(multiplexer_3_out), .sel(ASel));
  Multiplexer #(.width(32), .enable("false")) multiplexer_4 (
    .in0(read_data_2), .in1(imm), .out(multiplexer_4_out), .sel(BSel));
  alu_main main_2 (
    .Switch(ALUSel), .X(multiplexer_3_out), .Result(undone_alu_output), .Y(multiplexer_4_out));  // open: Equal
  // Probe on multiplexer_4_out
  Multiplexer #(.width(32), .enable("false")) multiplexer_5 (
    .in0(alu_output), .in1(shifter_2_out), .out(multiplexer_5_out), .sel(isSWGE));
  Shifter #(.width(32), .shift("lr")) shifter_2 (.in(read_data_1), .\dist (5'b00010), .out(shifter_2_out));
  Detr_S_Type__Store detr_s_type_store_1 (.rs2(read_data_2), .isSW(isSW), .isSWGE(isSWGE), .imm(imm), .MemRW(MemRW));
  // Probe on mem
  // mem_main MEM: pin names not known; wires that end beside it: multiplexer_5_out, read_data_2, MemRW, CLOCK, mem
  addressChange addresschange_1 (
    .load(load), .isSW(isSW), .raw_alu_output(undone_alu_output), .isLB(isLB), .isLH(isLH), .isLW(isLW),
    .address(alu_output));
  Adder #(.width(32)) adder_2 (.a(32'h4), .b(pc), .out(adder_2_out));  // open: cin, cout
  Multiplexer #(.select(2), .width(32), .enable("false")) multiplexer_6 (
    .in0(mem), .in1(alu_output), .in2(adder_2_out), .out(write_back), .sel(WBSel));  // open: in3

  // Other names for the same wires on the sheet: a0[31:0] = a0_Value; clk = CLOCK; fetch_addr[31:0] = FETCH_ADDRESS;
  //   rd[4:0] = instruction_t[11:7]; rs1[4:0] = instruction_t[19:15]; rs2[4:0] = instruction_t[24:20];
  //   ra[31:0] = ra_Value; s0[31:0] = s0_Value; s1[31:0] = s1_Value; sp[31:0] = sp_Value; t0[31:0] = t0_Value;
  //   t1[31:0] = t1_Value; t2[31:0] = t2_Value

  // Notes on the sheet:
  //   Output
  //   These are outputs/inputs from run.circ
  //   Inputs
endmodule

module R_Type (
  input  [31:0] instruction,
  output [6:0] opcode,
  output [4:0] rd,
  output [2:0] func3,
  output [4:0] rs1,
  output [4:0] rs2,
  output [6:0] func7
);


  assign func3 = instruction[14:12];
  assign func7 = instruction[31:25];
  assign opcode = instruction[6:0];
  assign rd = instruction[11:7];
  assign rs1 = instruction[19:15];
  assign rs2 = instruction[24:20];
endmodule

module Opcode (
  input  [31:0] instruction,
  output rtype,
  output load,
  output i_type__no_load,
  output store,
  output sb_type,
  output u_type__LUI,
  output uj_type__JAL,
  output i_type__JALR
);

  Comparator #(.width(7)) comparator_1 (.a(instruction[6:0]), .b(7'b0110011), .eq(rtype));  // open: gt, lt
  Comparator #(.width(7)) comparator_2 (.a(instruction[6:0]), .b(7'b0000011), .eq(load));  // open: gt, lt
  Comparator #(.width(7)) comparator_3 (.a(instruction[6:0]), .b(7'b0010011), .eq(i_type__no_load));  // open: gt, lt
  Comparator #(.width(7)) comparator_4 (.a(instruction[6:0]), .b(7'b0100011), .eq(store));  // open: gt, lt
  Comparator #(.width(7)) comparator_5 (.a(instruction[6:0]), .b(7'b1100011), .eq(sb_type));  // open: gt, lt
  Comparator #(.width(7)) comparator_6 (.a(instruction[6:0]), .b(7'b0110111), .eq(u_type__LUI));  // open: gt, lt
  Comparator #(.width(7)) comparator_7 (.a(instruction[6:0]), .b(7'b1101111), .eq(uj_type__JAL));  // open: gt, lt
  Comparator #(.width(7)) comparator_8 (.a(instruction[6:0]), .b(7'b1100111), .eq(i_type__JALR));  // open: gt, lt
endmodule

// I-Type
module I_Type_except_LoadT (
  input  [31:0] instruction,
  output [6:0] opcode,
  output [4:0] rd,
  output [2:0] func3,
  output [4:0] rs1,
  output [11:0] imm12
);


  assign func3 = instruction[14:12];
  assign imm12 = instruction[31:20];
  assign opcode = instruction[6:0];
  assign rd = instruction[11:7];
  assign rs1 = instruction[19:15];
endmodule

// Load
module I_Type__Load (
  input  [31:0] instruction,
  output [6:0] opcode,
  output [4:0] rd,
  output [2:0] func3,
  output [4:0] rs1,
  output [11:0] imm12
);


  assign func3 = instruction[14:12];
  assign imm12 = instruction[31:20];
  assign opcode = instruction[6:0];
  assign rd = instruction[11:7];
  assign rs1 = instruction[19:15];
endmodule

// LUI
module U_Type__LUI (
  input  [31:0] instruction,
  output [6:0] opcode,
  output [4:0] rd,
  output [19:0] imm20
);


  assign imm20 = instruction[31:12];
  assign opcode = instruction[6:0];
  assign rd = instruction[11:7];
endmodule

// JAL
module UJ_Type__JAL (
  input  [31:0] instruction,
  output [6:0] opcode,
  output [4:0] rd,
  output [19:0] imm20
);


  assign imm20 = instruction[31:12];
  assign opcode = instruction[6:0];
  assign rd = instruction[11:7];
endmodule

// JALR
module I_Type__JALR (
  input  [31:0] instruction,
  output [6:0] opcode,
  output [4:0] rd,
  output [2:0] func3,
  output [4:0] rs1,
  output [11:0] imm12
);


  assign func3 = instruction[14:12];
  assign imm12 = instruction[31:20];
  assign opcode = instruction[6:0];
  assign rd = instruction[11:7];
  assign rs1 = instruction[19:15];
endmodule

module Detr_R_Type (
  input  [2:0] func3,
  input  [6:0] func7,
  output [3:0] alu_sel
);

  wire add, add_op, \and , div, func3_is_0, func3_is_1, func3_is_2, func3_is_4, func3_is_5, func3_is_6,
       func3_is_7, mul, mulh, \or , rem, sll, slt, srl, sub, \xor ;
  wire [3:0] add_switch, and_switch, div_switch, mulh_switch, mult_switch, or_switch, rem_switch, result,
       sll_switch, slt_switch, srl_switch, sub_switch, xor_switch;
  wire [6:0] f3_is_0_and_f7_5, f3_is_1_and_f7_5, f3_is_2_and_f7_5, f3_is_4_and_f7_5, f3_is_5_and_f7_5,
       f3_is_6_and_f7_5, f3_is_7_and_f7_5;

  Comparator #(.width(3), .mode("unsigned")) comparator_1 (.a(func3), .b(3'b000), .eq(func3_is_0));  // open: gt, lt
  Comparator #(.width(3), .mode("unsigned")) comparator_2 (.a(func3), .b(3'b001), .eq(func3_is_1));  // open: gt, lt
  Comparator #(.width(3), .mode("unsigned")) comparator_3 (.a(func3), .b(3'b010), .eq(func3_is_2));  // open: gt, lt
  Comparator #(.width(3), .mode("unsigned")) comparator_4 (.a(func3), .b(3'b100), .eq(func3_is_4));  // open: gt, lt
  Comparator #(.width(3), .mode("unsigned")) comparator_5 (.a(func3), .b(3'b101), .eq(func3_is_5));  // open: gt, lt
  Comparator #(.width(3), .mode("unsigned")) comparator_6 (.a(func3), .b(3'b110), .eq(func3_is_6));  // open: gt, lt
  Comparator #(.width(3), .mode("unsigned")) comparator_7 (.a(func3), .b(3'b111), .eq(func3_is_7));  // open: gt, lt
  Multiplexer #(.width(7), .enable("false")) multiplexer_1 (
    .in0(7'b0000101), .in1(func7), .out(f3_is_0_and_f7_5), .sel(func3_is_0));
  Multiplexer #(.width(7), .enable("false")) multiplexer_2 (
    .in0(7'b0000101), .in1(func7), .out(f3_is_1_and_f7_5), .sel(func3_is_1));
  Multiplexer #(.width(7), .enable("false")) multiplexer_3 (
    .in0(7'b0000101), .in1(func7), .out(f3_is_2_and_f7_5), .sel(func3_is_2));
  Multiplexer #(.width(7), .enable("false")) multiplexer_4 (
    .in0(7'b0000101), .in1(func7), .out(f3_is_4_and_f7_5), .sel(func3_is_4));
  Multiplexer #(.width(7), .enable("false")) multiplexer_5 (
    .in0(7'b0000101), .in1(func7), .out(f3_is_5_and_f7_5), .sel(func3_is_5));
  Multiplexer #(.width(7), .enable("false")) multiplexer_6 (
    .in0(7'b0000101), .in1(func7), .out(f3_is_6_and_f7_5), .sel(func3_is_6));
  Multiplexer #(.width(7), .enable("false")) multiplexer_7 (
    .in0(7'b0000101), .in1(func7), .out(f3_is_7_and_f7_5), .sel(func3_is_7));
  Comparator #(.width(7), .mode("unsigned")) comparator_8 (
    .a(f3_is_0_and_f7_5), .b({7{1'b0}}), .eq(add));  // open: gt, lt
  Comparator #(.width(7), .mode("unsigned")) comparator_9 (
    .a(f3_is_0_and_f7_5), .b(7'b0000001), .eq(mul));  // open: gt, lt
  Comparator #(.width(7), .mode("unsigned")) comparator_10 (
    .a(f3_is_0_and_f7_5), .b(7'b0100000), .eq(sub));  // open: gt, lt
  Comparator #(.width(7), .mode("unsigned")) comparator_11 (
    .a(f3_is_1_and_f7_5), .b({7{1'b0}}), .eq(sll));  // open: gt, lt
  Comparator #(.width(7), .mode("unsigned")) comparator_12 (
    .a(f3_is_1_and_f7_5), .b(7'b0000001), .eq(mulh));  // open: gt, lt
  Comparator #(.width(7), .mode("unsigned")) comparator_13 (
    .a(f3_is_2_and_f7_5), .b({7{1'b0}}), .eq(slt));  // open: gt, lt
  Comparator #(.width(7), .mode("unsigned")) comparator_14 (
    .a(f3_is_4_and_f7_5), .b({7{1'b0}}), .eq(\xor ));  // open: gt, lt
  Comparator #(.width(7), .mode("unsigned")) comparator_15 (
    .a(f3_is_4_and_f7_5), .b(7'b0000001), .eq(div));  // open: gt, lt
  Comparator #(.width(7), .mode("unsigned")) comparator_16 (
    .a(f3_is_5_and_f7_5), .b({7{1'b0}}), .eq(srl));  // open: gt, lt
  Comparator #(.width(7), .mode("unsigned")) comparator_17 (
    .a(f3_is_6_and_f7_5), .b({7{1'b0}}), .eq(\or ));  // open: gt, lt
  Comparator #(.width(7), .mode("unsigned")) comparator_18 (
    .a(f3_is_6_and_f7_5), .b(7'b0000001), .eq(rem));  // open: gt, lt
  Comparator #(.width(7), .mode("unsigned")) comparator_19 (
    .a(f3_is_7_and_f7_5), .b({7{1'b0}}), .eq(\and ));  // open: gt, lt
  Multiplexer #(.width(4), .enable("false")) multiplexer_8 (.in0(4'b0000), .in1(4'b0000), .out(add_switch), .sel(add));
  Multiplexer #(.width(4), .enable("false")) multiplexer_9 (.in0(4'b0000), .in1(4'b1010), .out(mult_switch), .sel(mul));
  Multiplexer #(.width(4), .enable("false")) multiplexer_10 (.in0(4'b0000), .in1(4'b1100), .out(sub_switch), .sel(sub));
  Multiplexer #(.width(4), .enable("false")) multiplexer_11 (.in0(4'b0000), .in1(4'b0110), .out(sll_switch), .sel(sll));
  Multiplexer #(.width(4), .enable("false")) multiplexer_12 (
    .in0(4'b0000), .in1(4'b1011), .out(mulh_switch), .sel(mulh));
  Multiplexer #(.width(4), .enable("false")) multiplexer_13 (.in0(4'b0000), .in1(4'b0111), .out(slt_switch), .sel(slt));
  Multiplexer #(.width(4), .enable("false")) multiplexer_14 (
    .in0(4'b0000), .in1(4'b0011), .out(xor_switch), .sel(\xor ));
  Multiplexer #(.width(4), .enable("false")) multiplexer_15 (.in0(4'b0000), .in1(4'b1000), .out(div_switch), .sel(div));
  Multiplexer #(.width(4), .enable("false")) multiplexer_16 (.in0(4'b0000), .in1(4'b0100), .out(srl_switch), .sel(srl));
  Multiplexer #(.width(4), .enable("false")) multiplexer_17 (.in0(4'b0000), .in1(4'b0010), .out(or_switch), .sel(\or ));
  Multiplexer #(.width(4), .enable("false")) multiplexer_18 (.in0(4'b0000), .in1(4'b1001), .out(rem_switch), .sel(rem));
  Multiplexer #(.width(4), .enable("false")) multiplexer_19 (
    .in0(4'b0000), .in1(4'b0001), .out(and_switch), .sel(\and ));
  assign result = add_switch | mult_switch | sub_switch | sll_switch | mulh_switch | slt_switch | xor_switch | div_switch | srl_switch | or_switch | rem_switch | and_switch;  // OR_Gate or_1, 4 bits wide
  Comparator #(.width(4), .mode("unsigned")) comparator_20 (.a(result), .b(4'b0000), .eq(add_op));  // open: gt, lt
  Multiplexer #(.width(4), .enable("false")) multiplexer_20 (.in0(result), .in1(4'b0000), .out(alu_sel), .sel(add_op));

  // Notes on the sheet:
  //   Determines what func3 is
  //   func7 or 5 will come out, 5 is arbitrary since the constant != 0 
  //   Determine which alu operation it is
  //   Determine switch value for alu
endmodule

module Detr_S_Type__Store (
  input  [31:0] rs2,
  input  isSW,
  input  isSWGE,
  input  [31:0] imm,
  output MemRW
);

  wire and_1_out, comparator_1_eq, comparator_1_gt, condition;
  wire [31:0] imm_t;

  Bit_Extender #(.in_width(32), .out_width(32), .\type ("sign")) bit_extender_1 (.in(imm), .out(imm_t));
  Comparator #(.width(32)) comparator_1 (.a(rs2), .b(imm_t), .gt(comparator_1_gt), .eq(comparator_1_eq));  // open: lt
  or or_1 (condition, comparator_1_gt, comparator_1_eq);
  and and_1 (and_1_out, isSWGE, condition);
  or or_2 (MemRW, and_1_out, isSW);
endmodule

module Detr_SB_Type (
  input  [2:0] func3,
  output [1:0] Branch
);

  wire BrEq, BrLt, BrLTU;
  wire [1:0] multiplexer_1_out, multiplexer_2_out, multiplexer_3_out;

  Comparator #(.width(3), .mode("unsigned")) comparator_1 (.a(func3), .b(3'b000), .eq(BrEq));  // open: gt, lt
  Comparator #(.width(3)) comparator_2 (.a(func3), .b(3'b100), .eq(BrLt));  // open: gt, lt
  Comparator #(.width(3)) comparator_3 (.a(func3), .b(3'b110), .eq(BrLTU));  // open: gt, lt
  Multiplexer #(.width(2), .enable("false")) multiplexer_1 (
    .in0(2'b00), .in1(2'b00), .out(multiplexer_1_out), .sel(BrEq));
  Multiplexer #(.width(2), .enable("false")) multiplexer_2 (
    .in0(2'b00), .in1(2'b01), .out(multiplexer_2_out), .sel(BrLt));
  Multiplexer #(.width(2), .enable("false")) multiplexer_3 (
    .in0(2'b00), .in1(2'b10), .out(multiplexer_3_out), .sel(BrLTU));
  assign Branch = multiplexer_1_out | multiplexer_2_out | multiplexer_3_out;  // OR_Gate or_1, 2 bits wide
endmodule

module Store (
  input  [31:0] instruction,
  output [6:0] opcode,
  output [4:0] imm5,
  output [2:0] func3,
  output [4:0] rs1,
  output [4:0] rs2,
  output [6:0] imm7
);


  assign func3 = instruction[14:12];
  assign imm5 = instruction[11:7];
  assign imm7 = instruction[31:25];
  assign opcode = instruction[6:0];
  assign rs1 = instruction[19:15];
  assign rs2 = instruction[24:20];
endmodule

module SB_Type (
  input  [31:0] instruction,
  output [6:0] opcode,
  output [4:0] imm5,
  output [2:0] func3,
  output [4:0] rs1,
  output [4:0] rs2,
  output [6:0] imm7
);


  assign func3 = instruction[14:12];
  assign imm5 = instruction[11:7];
  assign imm7 = instruction[31:25];
  assign opcode = instruction[6:0];
  assign rs1 = instruction[19:15];
  assign rs2 = instruction[24:20];
endmodule

module Control_Panel (
  input  BrEq,
  input  BrLt,
  input  [31:0] instruction,
  output PCSel,
  output [2:0] ImmSel,
  output RegWEn,
  output BSel,
  output ASel,
  output [3:0] ALUSel,
  output MemRW_TBD,
  output [1:0] WBSel,
  output load,
  output store,
  output BrUn,
  output isSWGE,
  output isSW,
  output isLB,
  output isLH,
  output isLW
);

  wire itype, jal, jalr, lui, or_2_out, or_6_out, rtype, sbtype;
  wire [1:0] bit_extender_1_out, branch, jal_or_jalr, multiplexer_3_out, multiplexer_4_out,
       multiplexer_5_out, multiplexer_6_out, multiplexer_7_out, multiplexer_8_out, result, rtype_or_itype;
  wire [2:0] func3;

  ParseInstruction parseinstruction_1 (
    .instruction(instruction), .rtype(rtype), .load(load), .itype(itype), .store(store), .sbtype(sbtype),
    .lui(lui), .jal(jal), .jalr(jalr), .isSW(isSW), .isSWGE(isSWGE), .ALUSel(ALUSel), .func3(func3),
    .isLB(isLB), .isLH(isLH), .isLW(isLW));
  Opcode opcode_1 (
    .instruction(instruction), .rtype(rtype), .load(load), .i_type__no_load(itype), .store(store),
    .sb_type(sbtype), .u_type__LUI(lui), .uj_type__JAL(jal), .i_type__JALR(jalr));
  PCSelGen pcselgen_1 (
    .BrLt(BrLt), .BrEq(BrEq), .jal(jal), .jalr(jalr), .sbtype(sbtype), .Branch(branch), .PCSel(PCSel));
  Detr_SB_Type detr_sb_type_1 (.func3(func3), .Branch(branch));
  or or_1 (RegWEn, jalr, jal, lui, itype, load, rtype);
  BrUnGen brungen_1 (.sbtype(sbtype), .func3(func3), .BrUn(BrUn));
  ImmSelGen immselgen_1 (
    .load(load), .itype(itype), .store(store), .sbtype(sbtype), .lui(lui), .jal(jal), .jalr(jalr),
    .ImmSel(ImmSel));
  or or_2 (or_2_out, sbtype, jal);
  Multiplexer #(.enable("false")) multiplexer_1 (.in0(1'b0), .in1(1'b1), .out(ASel), .sel(or_2_out));
  Multiplexer #(.enable("false")) multiplexer_2 (.in0(1'b1), .in1(1'b0), .out(BSel), .sel(rtype));
  or or_3 (MemRW_TBD, isSW, isSWGE);
  Multiplexer #(.width(2), .enable("false")) multiplexer_3 (
    .in0(2'b00), .in1(2'b01), .out(multiplexer_3_out), .sel(itype));
  Multiplexer #(.width(2), .enable("false")) multiplexer_4 (
    .in0(2'b00), .in1(2'b01), .out(multiplexer_4_out), .sel(rtype));
  Multiplexer #(.width(2), .enable("false")) multiplexer_5 (
    .in0(2'b00), .in1(2'b10), .out(multiplexer_5_out), .sel(jal));
  Multiplexer #(.width(2), .enable("false")) multiplexer_6 (
    .in0(2'b00), .in1(2'b10), .out(multiplexer_6_out), .sel(jalr));
  assign rtype_or_itype = multiplexer_3_out | multiplexer_4_out;  // OR_Gate itype_or_rtype, 2 bits wide
  assign jal_or_jalr = multiplexer_5_out | multiplexer_6_out;  // OR_Gate or_4, 2 bits wide
  assign bit_extender_1_out = {{1{1'b0}}, lui};  // Bit_Extender bit_extender_1
  assign result = rtype_or_itype | jal_or_jalr | bit_extender_1_out;  // OR_Gate or_5, 2 bits wide
  Multiplexer #(.width(2), .enable("false")) multiplexer_7 (
    .in0(result), .in1(2'b00), .out(multiplexer_7_out), .sel(load));
  or or_6 (or_6_out, jal, jalr);
  assign WBSel = multiplexer_7_out | multiplexer_8_out;  // OR_Gate or_7, 2 bits wide
  Multiplexer #(.width(2), .enable("false")) multiplexer_8 (
    .in0(2'b00), .in1(2'b10), .out(multiplexer_8_out), .sel(or_6_out));

  // Notes on the sheet:
  //   Determines value to RegWEn
  //   ASel is calculated here
  //   BSel is calculated
  //   Determines whether to write or read
  //   Everything right of here outputs the WBSel
endmodule

module InstructDecode (
  input  [31:0] instruction
);

  wire opcode_1_i_type__jalr, opcode_1_i_type__no_load, opcode_1_load, opcode_1_rtype, opcode_1_sb_type,
       opcode_1_store, opcode_1_u_type__lui, opcode_1_uj_type__jal;

  Opcode opcode_1 (
    .instruction(instruction), .rtype(opcode_1_rtype), .load(opcode_1_load),
    .i_type__no_load(opcode_1_i_type__no_load), .store(opcode_1_store), .sb_type(opcode_1_sb_type),
    .u_type__LUI(opcode_1_u_type__lui), .uj_type__JAL(opcode_1_uj_type__jal),
    .i_type__JALR(opcode_1_i_type__jalr));
  R_Type r_type_1 (.instruction(instruction));  // open: opcode, rd, func3, rs1, rs2, func7
  I_Type_except_LoadT i_type_except_loadt_1 (.instruction(instruction));  // open: opcode, rd, func3, rs1, imm12
  I_Type__Load i_type_load_1 (.instruction(instruction));  // open: opcode, rd, func3, rs1, imm12
  Store store_1 (.instruction(instruction));  // open: opcode, imm5, func3, rs1, rs2, imm7
  SB_Type sb_type_1 (.instruction(instruction));  // open: opcode, imm5, func3, rs1, rs2, imm7
  UJ_Type__JAL uj_type_jal_1 (.instruction(instruction));  // open: opcode, rd, imm20
  U_Type__LUI u_type_lui_1 (.instruction(instruction));  // open: opcode, rd, imm20
  I_Type__JALR i_type_jalr_1 (.instruction(instruction));  // open: opcode, rd, func3, rs1, imm12
endmodule

// imm gen
module ImmGen (
  input  [24:0] _25bit,
  input  [2:0] immSel,
  output [31:0] Imm
);

  wire [11:0] shifter_1_out;
  wire [19:0] shifter_2_out;
  wire [24:0] parse_i_type_imm, parse_jal_imm, parse_jalr_imm, parse_load_imm, parse_lui_imm,
       parse_sb_type_imm, parse_store_imm;
  wire [31:0] parsed_i_type, parsed_jal, parsed_jalr, parsed_load, parsed_sb_type, parsed_store;

  Demultiplexer #(.select(3), .width(25), .enable("false")) demultiplexer_1 (
    .out0(parse_i_type_imm), .out1(parse_load_imm), .out2(parse_jalr_imm), .out3(parse_store_imm),
    .out4(parse_sb_type_imm), .out5(parse_lui_imm), .out6(parse_jal_imm), .in(_25bit), .sel(immSel));  // open: out7
  assign parsed_i_type = {{20{parse_i_type_imm[24]}}, parse_i_type_imm[24:13]};  // Bit_Extender bit_extender_1
  assign parsed_load = {{20{parse_load_imm[24]}}, parse_load_imm[24:13]};  // Bit_Extender bit_extender_2
  assign parsed_jalr = {{20{parse_jalr_imm[24]}}, parse_jalr_imm[24:13]};  // Bit_Extender bit_extender_3
  assign parsed_store = {{20{parse_store_imm[24]}}, {parse_store_imm[24:18], parse_store_imm[4:0]}};  // Bit_Extender bit_extender_4
  Shifter #(.width(12)) shifter_1 (
    .in({parse_sb_type_imm[24], parse_sb_type_imm[0], parse_sb_type_imm[23:18], parse_sb_type_imm[4:1]}),
    .\dist (4'b0001), .out(shifter_1_out));
  Shifter #(.width(20)) shifter_2 (
    .in({parse_jal_imm[24], parse_jal_imm[12:5], parse_jal_imm[13], parse_jal_imm[23:14]}),
    .\dist (5'b00001), .out(shifter_2_out));
  assign parsed_sb_type = {{20{shifter_1_out[11]}}, shifter_1_out};  // Bit_Extender bit_extender_5
  assign parsed_jal = {{12{shifter_2_out[19]}}, shifter_2_out};  // Bit_Extender bit_extender_6
  assign Imm = parsed_i_type | parsed_load | parsed_jalr | parsed_store | parsed_sb_type | {parse_lui_imm[24:5], {12{1'b0}}} | parsed_jal;  // OR_Gate or_1, 32 bits wide

  // Other names for the same wires on the sheet: parsed_lui[31:12] = parse_lui_imm[24:5]; unparsed[24:0] = _25bit

  // Notes on the sheet:
  //   Take imm and reassemble it
endmodule

module ImmSelGen (
  input  load,
  input  itype,
  input  store,
  input  sbtype,
  input  lui,
  input  jal,
  input  jalr,
  output [2:0] ImmSel
);

  wire [2:0] itypeImmSel, jalImmSel, jalrImmSel, loadImmSel, luiImmSel, sbtypeImmSel, storeImmSel;

  Multiplexer #(.width(3), .enable("false")) multiplexer_1 (.in0(3'b000), .in1(3'b001), .out(loadImmSel), .sel(load));
  Multiplexer #(.width(3), .enable("false")) multiplexer_2 (.in0(3'b000), .in1(3'b000), .out(itypeImmSel), .sel(itype));
  Multiplexer #(.width(3), .enable("false")) multiplexer_3 (.in0(3'b000), .in1(3'b011), .out(storeImmSel), .sel(store));
  Multiplexer #(.width(3), .enable("false")) multiplexer_4 (
    .in0(3'b000), .in1(3'b100), .out(sbtypeImmSel), .sel(sbtype));
  Multiplexer #(.width(3), .enable("false")) multiplexer_5 (.in0(3'b000), .in1(3'b101), .out(luiImmSel), .sel(lui));
  Multiplexer #(.width(3), .enable("false")) multiplexer_6 (.in0(3'b000), .in1(3'b110), .out(jalImmSel), .sel(jal));
  Multiplexer #(.width(3), .enable("false")) multiplexer_7 (.in0(3'b000), .in1(3'b010), .out(jalrImmSel), .sel(jalr));
  assign ImmSel = loadImmSel | itypeImmSel | storeImmSel | sbtypeImmSel | luiImmSel | jalImmSel | jalrImmSel;  // OR_Gate or_1, 3 bits wide
endmodule

module ALUSelGen (
  input  jalr,
  input  jalr_2,
  input  jalr_3,
  input  jalr_4,
  input  jalr_5,
  input  jalr_6,
  input  jalr_7,
  input  jalr_8
);
endmodule

module PCSelGen (
  input  BrLt,
  input  BrEq,
  input  jal,
  input  jalr,
  input  sbtype,
  input  [1:0] Branch,
  output PCSel
);

  wire and_1_out, and_2_out, and_3_out, and_4_out, and_5_out, and_6_out, comparator_1_eq, comparator_2_eq,
       comparator_3_eq;

  Comparator #(.width(2), .mode("unsigned")) comparator_1 (
    .a(2'b00), .b(Branch), .eq(comparator_1_eq));  // open: gt, lt
  Comparator #(.width(2), .mode("unsigned")) comparator_2 (
    .a(2'b01), .b(Branch), .eq(comparator_2_eq));  // open: gt, lt
  Comparator #(.width(2), .mode("unsigned")) comparator_3 (
    .a(2'b10), .b(Branch), .eq(comparator_3_eq));  // open: gt, lt
  and and_1 (and_1_out, BrEq, comparator_1_eq);
  and and_2 (and_2_out, BrLt, comparator_2_eq);
  and and_3 (and_3_out, BrLt, comparator_3_eq);
  and and_4 (and_4_out, sbtype, and_1_out);
  and and_5 (and_5_out, sbtype, and_2_out);
  and and_6 (and_6_out, sbtype, and_3_out);
  or or_1 (PCSel, and_4_out, jal, and_5_out, jalr, and_6_out);
endmodule

module ParseInstruction (
  input  [31:0] instruction,
  input  rtype,
  input  load,
  input  itype,
  input  store,
  input  sbtype,
  input  lui,
  input  jal,
  input  jalr,
  output [3:0] ALUSel,
  output [2:0] func3,
  output isLB,
  output isLH,
  output isLW,
  output isSWGE,
  output isSW
);

  wire comparator_2_eq, comparator_4_eq, comparator_5_eq, comparator_6_eq, comparator_7_eq, or_2_out;
  wire [2:0] itype_func3, jalr_func3, load_func3, or_1_out, rtype_func3, sbtype_func3, store_func3;
  wire [3:0] itype_alusel, lui_alusel, rtype_alusel, swge_alusel;
  wire [6:0] r_type_1_func7;
  wire [31:0] multiplexer_1_out, multiplexer_2_out, multiplexer_3_out, multiplexer_4_out, multiplexer_5_out,
       multiplexer_6_out, multiplexer_7_out, multiplexer_8_out;

  Multiplexer #(.width(32), .enable("false")) multiplexer_1 (
    .in0({32{1'b0}}), .in1(instruction), .out(multiplexer_1_out), .sel(rtype));
  Multiplexer #(.width(32), .enable("false")) multiplexer_2 (
    .in0({32{1'b0}}), .in1(instruction), .out(multiplexer_2_out), .sel(load));
  Multiplexer #(.width(32), .enable("false")) multiplexer_3 (
    .in0({32{1'b0}}), .in1(instruction), .out(multiplexer_3_out), .sel(itype));
  Multiplexer #(.width(32), .enable("false")) multiplexer_4 (
    .in0({32{1'b0}}), .in1(instruction), .out(multiplexer_4_out), .sel(store));
  Multiplexer #(.width(32), .enable("false")) multiplexer_5 (
    .in0({32{1'b0}}), .in1(instruction), .out(multiplexer_5_out), .sel(sbtype));
  Multiplexer #(.width(32), .enable("false")) multiplexer_6 (
    .in0({32{1'b0}}), .in1(instruction), .out(multiplexer_6_out), .sel(lui));
  Multiplexer #(.width(32), .enable("false")) multiplexer_7 (
    .in0({32{1'b0}}), .in1(instruction), .out(multiplexer_7_out), .sel(jal));
  Multiplexer #(.width(32), .enable("false")) multiplexer_8 (
    .in0({32{1'b0}}), .in1(instruction), .out(multiplexer_8_out), .sel(jalr));
  R_Type r_type_1 (
    .instruction(multiplexer_1_out), .func3(rtype_func3), .func7(r_type_1_func7));  // open: opcode, rd, rs1, rs2
  I_Type__Load i_type_load_1 (.instruction(multiplexer_2_out), .func3(load_func3));  // open: opcode, rd, rs1, imm12
  I_Type_except_LoadT i_type_except_loadt_1 (
    .instruction(multiplexer_3_out), .func3(itype_func3));  // open: opcode, rd, rs1, imm12
  Store store_1 (.instruction(multiplexer_4_out), .func3(store_func3));  // open: opcode, imm5, rs1, rs2, imm7
  SB_Type sb_type_1 (.instruction(multiplexer_5_out), .func3(sbtype_func3));  // open: opcode, imm5, rs1, rs2, imm7
  U_Type__LUI u_type_lui_1 (.instruction(multiplexer_6_out));  // open: opcode, rd, imm20
  UJ_Type__JAL uj_type_jal_1 (.instruction(multiplexer_7_out));  // open: opcode, rd, imm20
  I_Type__JALR i_type_jalr_1 (.instruction(multiplexer_8_out), .func3(jalr_func3));  // open: opcode, rd, rs1, imm12
  Detr_R_Type detr_r_type_1 (.func3(rtype_func3), .func7(r_type_1_func7), .alu_sel(rtype_alusel));
  Comparator #(.width(3), .mode("unsigned")) comparator_1 (.a(load_func3), .b(3'b000), .eq(isLB));  // open: gt, lt
  Detr_I_Type__General detr_i_type_general_1 (.func3(itype_func3), .alu_sel(itype_alusel));
  Comparator #(.width(1), .mode("unsigned")) comparator_2 (.a(lui), .b(1'b0), .eq(comparator_2_eq));  // open: gt, lt
  Comparator #(.width(3), .mode("unsigned")) comparator_3 (.a(load_func3), .b(3'b010), .eq(isLW));  // open: gt, lt
  assign or_1_out = itype_func3 | load_func3 | rtype_func3 | store_func3 | sbtype_func3 | jalr_func3;  // OR_Gate or_1, 3 bits wide
  Multiplexer #(.width(4), .enable("false")) multiplexer_9 (
    .in0(4'b1110), .in1(4'b0000), .out(lui_alusel), .sel(comparator_2_eq));
  Comparator #(.width(1)) comparator_4 (.a(store), .b(1'b1), .eq(comparator_4_eq));  // open: gt, lt
  Comparator #(.width(3), .mode("unsigned")) comparator_5 (
    .a(store_func3), .b(3'b111), .eq(comparator_5_eq));  // open: gt, lt
  Comparator #(.width(1)) comparator_6 (.a(store), .b(1'b1), .eq(comparator_6_eq));  // open: gt, lt
  Comparator #(.width(3), .mode("unsigned")) comparator_7 (
    .a(store_func3), .b(3'b010), .eq(comparator_7_eq));  // open: gt, lt
  Comparator #(.width(3), .mode("unsigned")) comparator_8 (.a(load_func3), .b(3'b001), .eq(isLH));  // open: gt, lt
  Multiplexer #(.width(3), .enable("false")) multiplexer_10 (.in0(or_1_out), .in1(3'b011), .out(func3), .sel(or_2_out));
  or or_2 (or_2_out, jal, lui);
  and and_1 (isSWGE, comparator_4_eq, comparator_5_eq);
  and and_2 (isSW, comparator_6_eq, comparator_7_eq);
  Multiplexer #(.width(4), .enable("false")) multiplexer_11 (
    .in0(4'b0000), .in1(4'b1111), .out(swge_alusel), .sel(isSWGE));
  assign ALUSel = rtype_alusel | itype_alusel | lui_alusel | swge_alusel;  // OR_Gate or_3, 4 bits wide
endmodule

module Detr_I_Type__General (
  input  [2:0] func3,
  output [3:0] alu_sel
);

  wire addi, andi, ori, slli, slti, srli, xori;
  wire [3:0] addi_switch, andi_switch, or_switch, result, slli_switch, slti_switch, srl_switch, xor_switch;

  Comparator #(.width(3), .mode("unsigned")) comparator_1 (.a(func3), .b(3'b000), .eq(addi));  // open: gt, lt
  Comparator #(.width(3), .mode("unsigned")) comparator_2 (.a(func3), .b(3'b001), .eq(slli));  // open: gt, lt
  Comparator #(.width(3), .mode("unsigned")) comparator_3 (.a(func3), .b(3'b010), .eq(slti));  // open: gt, lt
  Comparator #(.width(3), .mode("unsigned")) comparator_4 (.a(func3), .b(3'b100), .eq(xori));  // open: gt, lt
  Comparator #(.width(3), .mode("unsigned")) comparator_5 (.a(func3), .b(3'b101), .eq(srli));  // open: gt, lt
  Comparator #(.width(3), .mode("unsigned")) comparator_6 (.a(func3), .b(3'b110), .eq(ori));  // open: gt, lt
  Comparator #(.width(3), .mode("unsigned")) comparator_7 (.a(func3), .b(3'b111), .eq(andi));  // open: gt, lt
  Multiplexer #(.width(4), .enable("false")) multiplexer_1 (
    .in0(4'b0000), .in1(4'b0000), .out(addi_switch), .sel(addi));
  Multiplexer #(.width(4), .enable("false")) multiplexer_2 (
    .in0(4'b0000), .in1(4'b0110), .out(slli_switch), .sel(slli));
  Multiplexer #(.width(4), .enable("false")) multiplexer_3 (
    .in0(4'b0000), .in1(4'b0111), .out(slti_switch), .sel(slti));
  Multiplexer #(.width(4), .enable("false")) multiplexer_4 (.in0(4'b0000), .in1(4'b0011), .out(xor_switch), .sel(xori));
  Multiplexer #(.width(4), .enable("false")) multiplexer_5 (.in0(4'b0000), .in1(4'b0100), .out(srl_switch), .sel(srli));
  Multiplexer #(.width(4), .enable("false")) multiplexer_6 (.in0(4'b0000), .in1(4'b0010), .out(or_switch), .sel(ori));
  Multiplexer #(.width(4), .enable("false")) multiplexer_7 (
    .in0(4'b0000), .in1(4'b0001), .out(andi_switch), .sel(andi));
  assign result = addi_switch | slli_switch | slti_switch | xor_switch | srl_switch | or_switch | andi_switch;  // OR_Gate or_1, 4 bits wide
  Multiplexer #(.width(4), .enable("false")) multiplexer_8 (.in0(result), .in1(4'b0000), .out(alu_sel), .sel(addi));

  // Notes on the sheet:
  //   Determines what func3 is
endmodule

module addressChange (
  input  load,
  input  isSW,
  input  [31:0] raw_alu_output,
  input  isLB,
  input  isLH,
  input  isLW,
  output [31:0] address
);

  wire and_1_out, and_2_out, and_3_out, isLoad;
  wire [1:0] multiplexer_1_out, multiplexer_2_out, sel;
  wire [31:0] LB, LH, LoadAddress, multiplexer_4_out, multiplexer_5_out, multiplexer_6_out, or_3_out,
       shifted_address, shifter_2_out, shifter_4_out;

  and and_1 (and_1_out, load, isLB);
  and and_2 (and_2_out, load, isLH);
  and and_3 (and_3_out, load, isLW);
  Shifter #(.width(32), .shift("lr")) shifter_1 (.in(raw_alu_output), .\dist (5'b00010), .out(shifted_address));
  or or_1 (isLoad, and_1_out, and_2_out, and_3_out);
  Shifter #(.width(32)) shifter_2 (.in(raw_alu_output), .\dist (5'b11000), .out(shifter_2_out));
  Shifter #(.width(32), .shift("lr")) shifter_3 (.in(shifter_2_out), .\dist (5'b11000), .out(LB));
  Shifter #(.width(32)) shifter_4 (.in(raw_alu_output), .\dist (5'b10000), .out(shifter_4_out));
  Shifter #(.width(32), .shift("lr")) shifter_5 (.in(shifter_4_out), .\dist (5'b10000), .out(LH));
  Multiplexer #(.width(2), .enable("false")) multiplexer_1 (
    .in0(2'b00), .in1(2'b01), .out(multiplexer_1_out), .sel(isSW));
  Multiplexer #(.width(2), .enable("false")) multiplexer_2 (
    .in0(2'b00), .in1(2'b10), .out(multiplexer_2_out), .sel(isLoad));
  Multiplexer #(.select(2), .width(32), .enable("false")) multiplexer_3 (
    .in0(raw_alu_output), .in1(shifted_address), .in2(LoadAddress), .out(address), .sel(sel));  // open: in3
  assign sel = multiplexer_1_out | multiplexer_2_out;  // OR_Gate or_2, 2 bits wide
  Multiplexer #(.width(32), .enable("false")) multiplexer_4 (
    .in0({32{1'b0}}), .in1(LB), .out(multiplexer_4_out), .sel(isLB));
  Multiplexer #(.width(32), .enable("false")) multiplexer_5 (
    .in0({32{1'b0}}), .in1(LH), .out(multiplexer_5_out), .sel(isLH));
  Multiplexer #(.width(32), .enable("false")) multiplexer_6 (
    .in0({32{1'b0}}), .in1(raw_alu_output), .out(multiplexer_6_out), .sel(isLW));
  assign or_3_out = multiplexer_4_out | multiplexer_5_out | multiplexer_6_out;  // OR_Gate or_3, 32 bits wide
  Shifter #(.width(32), .shift("lr")) shifter_6 (.in(or_3_out), .\dist (5'b00010), .out(LoadAddress));

  // Other names for the same wires on the sheet: LW[31:0] = raw_alu_output; raw_instruction[31:0] = raw_alu_output
endmodule

module firstOp (
  input  [31:0] pc,
  output isItFirst
);

  Comparator #(.width(32), .mode("unsigned")) comparator_1 (.a(pc), .b({32{1'b0}}), .eq(isItFirst));  // open: gt, lt
endmodule

module BrUnGen (
  input  sbtype,
  input  [2:0] func3,
  output BrUn
);

  wire [1:0] branch;
  wire [2:0] multiplexer_1_out;

  Multiplexer #(.width(3), .enable("false")) multiplexer_1 (
    .in0(3'b000), .in1(func3), .out(multiplexer_1_out), .sel(sbtype));
  Detr_SB_Type detr_sb_type_1 (.func3(multiplexer_1_out), .Branch(branch));
  Multiplexer #(.select(2), .enable("false")) multiplexer_2 (
    .in0(1'b0), .in1(1'b0), .in2(1'b1), .out(BrUn), .sel(branch));  // open: in3
endmodule

module BrChoose (
  input  [31:0] read_data_1,
  input  [31:0] read_data_2,
  input  BrUn,
  output BrEq,
  output BrLt
);

  wire SignedLt, UnLt;

  Comparator #(.width(32)) comparator_1 (.a(read_data_1), .b(read_data_2), .eq(BrEq), .lt(SignedLt));  // open: gt
  Comparator #(.width(32), .mode("unsigned")) comparator_2 (
    .a(read_data_1), .b(read_data_2), .lt(UnLt));  // open: gt, eq
  Multiplexer #(.enable("false")) multiplexer_1 (.in0(SignedLt), .in1(UnLt), .out(BrLt), .sel(BrUn));
endmodule

module AmIJumping (
  input  sbtype,
  input  jal,
  input  BrEq,
  input  jalr,
  input  BrLt,
  input  [1:0] Branch,
  output Jumping
);

  wire and_1_out, and_2_out, and_3_out, and_4_out, and_5_out, and_6_out, comparator_1_eq, comparator_2_eq,
       comparator_3_eq;

  Comparator #(.width(2), .mode("unsigned")) comparator_1 (
    .a(2'b00), .b(Branch), .eq(comparator_1_eq));  // open: gt, lt
  Comparator #(.width(2), .mode("unsigned")) comparator_2 (
    .a(2'b01), .b(Branch), .eq(comparator_2_eq));  // open: gt, lt
  Comparator #(.width(2), .mode("unsigned")) comparator_3 (
    .a(2'b10), .b(Branch), .eq(comparator_3_eq));  // open: gt, lt
  and and_1 (and_1_out, BrEq, comparator_1_eq);
  and and_2 (and_2_out, BrLt, comparator_2_eq);
  and and_3 (and_3_out, BrLt, comparator_3_eq);
  and and_4 (and_4_out, sbtype, and_1_out);
  and and_5 (and_5_out, sbtype, and_2_out);
  and and_6 (and_6_out, sbtype, and_3_out);
  or or_1 (Jumping, and_4_out, jal, and_5_out, jalr, and_6_out);
endmodule
