// Logisim project alu.circ as structural Verilog
module main (
  input  [31:0] X,
  input  [31:0] Y,
  input  [3:0] Switch,
  output Equal,
  output [31:0] Result
);

  wire comparator_1_lt;
  wire [4:0] bitselector_1_out, bitselector_2_out, bitselector_3_out;
  wire [31:0] ADD, AND, Divider, LUI, MULH, MULT, OR, Remainder, shifter_2_out, SLL, SLT, SRA, SRL, SUB, XOR;

  Adder #(.width(32)) adder_1 (.a(X), .b(Y), .out(ADD));  // open: cin, cout
  BitSelector #(.width(32), .group(5)) bitselector_1 (.in(Y), .out(bitselector_1_out), .sel(3'b000));
  Shifter #(.width(32)) shifter_1 (.in(X), .\dist (bitselector_1_out), .out(SLL));
  Subtractor #(.width(32)) subtractor_1 (.a(X), .b(Y), .out(SUB));  // open: bin, bout
  assign AND = X & Y;  // AND_Gate AND, 32 bits wide
  Comparator #(.width(32)) comparator_1 (.a(X), .b(Y), .eq(Equal), .lt(comparator_1_lt));  // open: gt
  assign SLT = {{31{1'b0}}, comparator_1_lt};  // Bit_Extender bit_extender_1
  assign OR = X | Y;  // OR_Gate OR, 32 bits wide
  Multiplexer #(.select(4), .width(32), .disabled(0), .enable("false")) multiplexer_1 (
    .in0(ADD), .in1(AND), .in2(OR), .in3(XOR), .in4(SRL), .in5(SRA), .in6(SLL), .in7(SLT), .in8(Divider),
    .in9(Remainder), .in10(MULT), .in11(MULH), .in12(SUB), .in13({32{1'b0}}), .in14(LUI), .in15(X),
    .out(Result), .sel(Switch));
  Divider #(.width(32)) divider_1 (.a(X), .b(Y), .out(Divider));  // open: upper, rem
  Shifter #(.width(32), .shift("lr")) shifter_2 (.in(Y), .\dist (5'b01100), .out(shifter_2_out));
  assign XOR = X ^ Y;  // XOR_Gate XOR, 32 bits wide
  Shifter #(.width(32)) shifter_3 (.in(shifter_2_out), .\dist (5'b01100), .out(LUI));
  Divider #(.width(32)) divider_2 (.a(X), .b(Y), .rem(Remainder));  // open: out, upper
  BitSelector #(.width(32), .group(5)) bitselector_2 (.in(Y), .out(bitselector_2_out), .sel(3'b000));
  Shifter #(.width(32), .shift("lr")) shifter_4 (.in(X), .\dist (bitselector_2_out), .out(SRL));
  Multiplier #(.width(32)) multiplier_1 (.a(X), .b(Y), .out(MULT));  // open: cin, cout
  BitSelector #(.width(32), .group(5)) bitselector_3 (.in(Y), .out(bitselector_3_out), .sel(3'b000));
  Shifter #(.width(32), .shift("ar")) shifter_5 (.in(X), .\dist (bitselector_3_out), .out(SRA));
  Multiplier #(.width(32)) multiplier_2 (.a(X), .b(Y), .cout(MULH));  // open: out, cin

  // Other names for the same wires on the sheet: S[3:0] = Switch; SWGE[31:0] = X

  // Notes on the sheet:
  //   INPUTS to your circuit
  //   DON'T CHANGE THE LOCATIONS OF THE INPUTS AND OUTPUTS!
  //   OUTPUTS from your circuit
endmodule
