// Logisim project regfile.circ as structural Verilog: 1 circuit, main circuit main
module main (
  input  [4:0] Read_Register_1__rs1,
  input  [4:0] Read_Register_2__rs2,
  input  [4:0] Write_Register__rd,
  input  [31:0] Write_Data,
  input  Write_Enable,
  input  Clock,
  output [31:0] ra_Value,
  output [31:0] sp_Value,
  output [31:0] t0_Value,
  output [31:0] t1_Value,
  output [31:0] t2_Value,
  output [31:0] s0_Value,
  output [31:0] s1_Value,
  output [31:0] a0_Value,
  output [31:0] Read_Data_1,
  output [31:0] Read_Data_2
);

  wire a0_enable, a1_enable, ra_enable, s0_enable, s1_enable, sp_enable, t0_enable, t1_enable, t2_enable;
  wire [31:0] a1, zero;

  Demultiplexer #(.select(5), .disabled(0)) demultiplexer_1 (
    .out1(ra_enable), .out2(sp_enable), .out5(t0_enable), .out6(t1_enable), .out7(t2_enable),
    .out8(s0_enable), .out9(s1_enable), .out10(a0_enable), .out11(a1_enable), .in(Write_Enable),
    .sel(Write_Register__rd), .en(Write_Enable));  // open: out0, out3, out4, out12, out13, out14, out15, out16, out17, out18, out19, out20, out21, out22, out23, out24, out25, out26, out27, out28, out29, out30, out31
  Multiplexer #(.select(5), .width(32), .enable("false")) multiplexer_1 (
    .in0(zero), .in1(ra_Value), .in2(sp_Value), .in5(t0_Value), .in6(t1_Value), .in7(t2_Value),
    .in8(s0_Value), .in9(s1_Value), .in10(a0_Value), .in11(a1), .out(Read_Data_1), .sel(Read_Register_1__rs1));  // open: in3, in4, in12, in13, in14, in15, in16, in17, in18, in19, in20, in21, in22, in23, in24, in25, in26, in27, in28, in29, in30, in31
  Register #(.width(32)) u_zero (.Q(zero), .clk(Clock), .clr(1'b1));  // open: D, en
  Register #(.width(32)) t2 (.D(Write_Data), .en(t2_enable), .Q(t2_Value), .clk(Clock));  // open: clr
  Register #(.width(32)) ra (.D(Write_Data), .en(ra_enable), .Q(ra_Value), .clk(Clock));  // open: clr
  Register #(.width(32)) s0 (.D(Write_Data), .en(s0_enable), .Q(s0_Value), .clk(Clock));  // open: clr
  Multiplexer #(.select(5), .width(32), .enable("false")) multiplexer_2 (
    .in0(zero), .in1(ra_Value), .in2(sp_Value), .in5(t0_Value), .in6(t1_Value), .in7(t2_Value),
    .in8(s0_Value), .in9(s1_Value), .in10(a0_Value), .in11(a1), .out(Read_Data_2), .sel(Read_Register_2__rs2));  // open: in3, in4, in12, in13, in14, in15, in16, in17, in18, in19, in20, in21, in22, in23, in24, in25, in26, in27, in28, in29, in30, in31
  Register #(.width(32)) sp (.D(Write_Data), .en(sp_enable), .Q(sp_Value), .clk(Clock));  // open: clr
  Register #(.width(32)) s1 (.D(Write_Data), .en(s1_enable), .Q(s1_Value), .clk(Clock));  // open: clr
  Register #(.width(32)) t0 (.D(Write_Data), .en(t0_enable), .Q(t0_Value), .clk(Clock));  // open: clr
  Register #(.width(32)) a0 (.D(Write_Data), .en(a0_enable), .Q(a0_Value), .clk(Clock));  // open: clr
  Register #(.width(32)) t1 (.D(Write_Data), .en(t1_enable), .Q(t1_Value), .clk(Clock));  // open: clr
  Register #(.width(32)) u_a1 (.D(Write_Data), .en(a1_enable), .Q(a1), .clk(Clock));  // open: clr

  // Other names for the same wires on the sheet: a0[31:0] = a0_Value; clk = Clock; ra[31:0] = ra_Value;
  //   read_data1[31:0] = Read_Data_1; read_data2[31:0] = Read_Data_2; read_reg1[4:0] = Read_Register_1__rs1;
  //   read_reg2[4:0] = Read_Register_2__rs2; s0[31:0] = s0_Value; s1[31:0] = s1_Value; sp[31:0] = sp_Value;
  //   t0[31:0] = t0_Value; t1[31:0] = t1_Value; t2[31:0] = t2_Value; write_en = Write_Enable;
  //   write_reg[4:0] = Write_Register__rd

  // Notes on the sheet:
  //   INPUTS to your circuit
  //   These are DEBUG/TEST outputs from your circuit.
  //   OUTPUTS from your circuit
endmodule
